// Logisim project schematic.circ as structural Verilog: 9 circuits, main circuit main
// div_low
module main (
  input  [31:0] a,
  input  [31:0] b,
  input  rst,
  input  [3:0] aluop,
  input  output_inc,
  input  output_inverted,
  input  clk,
  output [31:0] res_low,
  output [31:0] res_high,
  output done
);

  wire add_c, comparator_1_eq, comparator_2_eq, comparator_4_lt, comparator_5_eq, comparator_6_eq, div_done,
       mul_done, multiplexer_3_out, or_2_out, or_3_out, or_4_out, or_5_out, or_6_out, or_7_out, or_8_out,
       start;
  wire [3:0] register_1_q, xor_2_out;
  wire [4:0] not_b, subtractor_2_out;
  wire [5:0] b_1, bit_extender_5_out, bit_extender_6_out, clo_circ_out1, clz_circ_out1, shifter_1_out;
  wire [31:0] add_s, and_1_out, bit_extender_1_out, bit_extender_2_out, bit_extender_3_out, high_div,
       high_sll, high_sra, low_div, low_rotr, low_sll, low_sra, low_srl, or_1_out, q, register_2_q,
       register_3_q, remainder, sub_s, subtractor_1_out, xor_1_out, xor_3_out, xor_4_out;
  wire [31:31] high_sub;
  wire [63:0] mul_circ_result, multiplexer_5_out, multiplexer_9_out, multiplexer_11_out, not_1_out, result,
       shifter_3_out, shifter_4_out, shifter_5_out, shifter_6_out, shifter_7_out, shifter_8_out;

  assign and_1_out = a & b;  // AND_Gate and_1, 32 bits wide
  assign or_1_out = a | b;  // OR_Gate or_1, 32 bits wide
  assign xor_1_out = a ^ b;  // XOR_Gate xor_1, 32 bits wide
  add_sub add (.c_in(aluop[0]), .sub_notAdd(aluop[0]), .in1(a), .in2(b), .s(add_s), .c(add_c));
  add_sub sub (.c_in(aluop[0]), .sub_notAdd(aluop[0]), .in1(a), .in2(b), .s(sub_s));  // open: c
  mul mul_circ (.multiplicand(a), .mutiplier(b), .clk(clk), .strat(start), .done(mul_done), .result(mul_circ_result));
  div div_circ (
    .clk(clk), .start(start), .dividend(a), .divisor(b), .remainder(remainder), .quotient(q), .done(div_done));
  clz clz_circ (.in1(a), .out1(clz_circ_out1));
  clo clo_circ (.in1(a), .out1(clo_circ_out1));
  assign bit_extender_1_out = {{26{1'b0}}, clo_circ_out1};  // Bit_Extender bit_extender_1
  assign bit_extender_2_out = {{26{1'b0}}, clz_circ_out1};  // Bit_Extender bit_extender_2
  Register #(.width(4)) register_1 (.D(aluop), .clk(clk), .Q(register_1_q));  // open: en, clr
  Comparator #(.width(4)) comparator_1 (.a(aluop), .b(4'b0010), .eq(comparator_1_eq));  // open: gt, lt
  Comparator #(.width(4)) comparator_2 (.a(aluop), .b(4'b0011), .eq(comparator_2_eq));  // open: gt, lt
  or or_2 (or_2_out, comparator_1_eq, comparator_2_eq);
  assign bit_extender_3_out = {{31{1'b0}}, add_c};  // Bit_Extender bit_extender_3
  Register #(.width(32)) register_2 (.D(a), .clk(clk), .Q(register_2_q));  // open: en, clr
  Register #(.width(32)) register_3 (.D(b), .clk(clk), .Q(register_3_q));  // open: en, clr
  assign xor_2_out = register_1_q ^ aluop;  // XOR_Gate xor_2, 4 bits wide
  Multiplexer #(.select(4), .width(32)) multiplexer_1 (
    .in0(add_s), .in1(sub_s), .in2(mul_circ_result[31:0]), .in3(low_div), .in4(and_1_out), .in5(or_1_out),
    .in6(xor_1_out), .in7(bit_extender_1_out), .in8(bit_extender_2_out), .in9(low_sll), .in10(low_srl),
    .in11(low_sra), .in12(low_rotr), .out(result[31:0]), .sel(aluop));  // open: in13, in14, in15
  Multiplexer #(.select(4), .width(32)) multiplexer_2 (
    .in0(bit_extender_3_out), .in1({32{high_sub[31]}}), .in2(mul_circ_result[63:32]), .in3(high_div),
    .in4({32{1'b0}}), .in5({32{1'b0}}), .in6({32{1'b0}}), .in7({32{1'b0}}), .in8({32{1'b0}}), .in9(high_sll),
    .in10({32{1'b0}}), .in11(high_sra), .in12({32{1'b0}}), .out(result[63:32]), .sel(aluop));  // open: in13, in14, in15
  assign xor_3_out = register_2_q ^ a;  // XOR_Gate xor_3, 32 bits wide
  Multiplexer multiplexer_3 (.in0(mul_done), .in1(div_done), .out(multiplexer_3_out), .sel(comparator_2_eq));
  assign xor_4_out = register_3_q ^ b;  // XOR_Gate xor_4, 32 bits wide
  or or_3 (or_3_out, xor_2_out[0], xor_2_out[1], xor_2_out[3], xor_2_out[2]);
  Multiplexer multiplexer_4 (.in0(1'b1), .in1(multiplexer_3_out), .out(done), .sel(or_2_out));
  or or_4 (or_4_out, xor_3_out[0], xor_3_out[1], xor_3_out[2], xor_3_out[3], xor_3_out[4], xor_3_out[5], xor_3_out[6], xor_3_out[7], xor_3_out[8], xor_3_out[9], xor_3_out[10], xor_3_out[11], xor_3_out[12], xor_3_out[13], xor_3_out[14], xor_3_out[15], xor_3_out[17], xor_3_out[18], xor_3_out[19], xor_3_out[20], xor_3_out[21], xor_3_out[22], xor_3_out[23], xor_3_out[24], xor_3_out[25], xor_3_out[26], xor_3_out[27], xor_3_out[28], xor_3_out[29], xor_3_out[30], xor_3_out[31], xor_3_out[16]);
  or or_5 (or_5_out, xor_4_out[0], xor_4_out[1], xor_4_out[2], xor_4_out[3], xor_4_out[4], xor_4_out[5], xor_4_out[6], xor_4_out[7], xor_4_out[8], xor_4_out[9], xor_4_out[10], xor_4_out[11], xor_4_out[12], xor_4_out[13], xor_4_out[14], xor_4_out[15], xor_4_out[17], xor_4_out[18], xor_4_out[19], xor_4_out[20], xor_4_out[21], xor_4_out[22], xor_4_out[23], xor_4_out[24], xor_4_out[25], xor_4_out[26], xor_4_out[27], xor_4_out[28], xor_4_out[29], xor_4_out[30], xor_4_out[31], xor_4_out[16]);
  Comparator #(.mode("unsigned"), .width(32)) comparator_3 (.a(a), .b(b), .lt(high_sub[31]));  // open: gt, eq
  Subtractor #(.width(32)) subtractor_1 (.a(b), .b(32'h1), .out(subtractor_1_out));  // open: bin, bout
  assign not_1_out = ~result;  // NOT_Gate not_1, 64 bits wide
  or or_6 (or_6_out, or_4_out, or_5_out, or_3_out);
  Shifter #(.width(6)) shifter_1 (.in(subtractor_1_out[5:0]), .\dist (3'b001), .out(shifter_1_out));
  Multiplexer #(.width(64)) multiplexer_5 (
    .in0(result), .in1(not_1_out), .out(multiplexer_5_out), .sel(output_inverted));
  Subtractor #(.width(5)) subtractor_2 (.a({5{1'b1}}), .b(b[4:0]), .out(subtractor_2_out));  // open: bin, bout
  and and_2 (start, or_6_out, or_2_out);
  Shifter #(.shift("lr"), .width(6)) shifter_2 (.in(shifter_1_out), .\dist (3'b001), .out(b_1));
  Adder #(.width(5)) adder_1 (.a(subtractor_2_out), .b(5'b00001), .out(not_b));  // open: cin, cout
  Adder #(.width(64)) adder_2 (
    .a(multiplexer_5_out), .b({{63{1'b0}}, output_inc}), .out({res_high, res_low}));  // open: cin, cout
  assign high_sra = {{31{a[31]}}, a[31]};  // Bit_Extender bit_extender_4
  Comparator #(.mode("unsigned"), .width(32)) comparator_4 (.a(a), .b(b), .lt(comparator_4_lt));  // open: gt, eq
  assign bit_extender_5_out = {{1{1'b0}}, b[4:0]};  // Bit_Extender bit_extender_5
  Multiplexer #(.width(32)) multiplexer_6 (.in0(remainder), .in1(a), .out(high_div), .sel(comparator_4_lt));
  Multiplexer #(.width(32)) multiplexer_7 (.in0(q), .in1({32{1'b0}}), .out(low_div), .sel(comparator_4_lt));
  Shifter #(.width(64)) shifter_3 (.in({{32{1'b0}}, a}), .\dist (bit_extender_5_out), .out(shifter_3_out));
  Shifter #(.shift("ar"), .width(64)) shifter_4 (.in({high_sra, a}), .\dist (b_1), .out(shifter_4_out));
  Shifter #(.shift("lr"), .width(64)) shifter_5 (.in(shifter_3_out), .\dist (6'b000001), .out(shifter_5_out));
  or or_7 (or_7_out, b[0], comparator_5_eq);
  Comparator #(.width(5)) comparator_5 (.a(b[4:0]), .b({5{1'b0}}), .eq(comparator_5_eq));  // open: gt, lt
  Multiplexer #(.width(64)) multiplexer_8 (
    .in0(shifter_5_out), .in1(shifter_3_out), .out({high_sll, low_sll}), .sel(or_7_out));
  Multiplexer #(.width(64)) multiplexer_9 (
    .in0(shifter_6_out), .in1(shifter_4_out), .out(multiplexer_9_out), .sel(b[0]));
  srlShift righeShift (.in1(a), .shift(b[4:0]), .out1(low_srl));
  Shifter #(.shift("ar"), .width(64)) shifter_6 (.in(shifter_4_out), .\dist (6'b000001), .out(shifter_6_out));
  Comparator #(.width(5)) comparator_6 (.a(b[4:0]), .b({5{1'b0}}), .eq(comparator_6_eq));  // open: gt, lt
  assign bit_extender_6_out = {{1{1'b0}}, not_b};  // Bit_Extender bit_extender_6
  Multiplexer #(.width(32)) multiplexer_10 (
    .in0(multiplexer_9_out[31:0]), .in1(a), .out(low_sra), .sel(comparator_6_eq));
  Shifter #(.width(64)) shifter_7 (.in({{32{1'b0}}, a}), .\dist (bit_extender_6_out), .out(shifter_7_out));
  Shifter #(.shift("lr"), .width(64)) shifter_8 (.in(shifter_7_out), .\dist (6'b000001), .out(shifter_8_out));
  or or_8 (or_8_out, not_b[0], comparator_5_eq);
  Multiplexer #(.width(64)) multiplexer_11 (
    .in0(shifter_8_out), .in1(shifter_7_out), .out(multiplexer_11_out), .sel(or_8_out));
  assign low_rotr = low_srl | multiplexer_11_out[31:0];  // OR_Gate or_9, 32 bits wide

  // Other names for the same wires on the sheet: lsb5_b[4:0] = b[4:0]; lsb_b = b[0];
  //   high_sub[30:0] = {31{high_sub[31]}}

  // Notes on the sheet:
  //   a: initial=0x139
endmodule

module clz (
  input  [31:0] in1,
  output [5:0] out1
);

  wire multiplexer_5_out, not_1_out, not_2_out;
  wire [1:0] multiplexer_4_out;
  wire [3:0] multiplexer_3_out;
  wire [4:0] nor_1_out;
  wire [5:0] bit_extender_1_out;
  wire [7:0] multiplexer_2_out;
  wire [15:0] multiplexer_1_out;

  Comparator #(.mode("unsigned"), .width(16)) comparator_1 (
    .a(in1[31:16]), .b({16{1'b0}}), .eq(nor_1_out[4]));  // open: gt, lt
  Multiplexer #(.width(16)) multiplexer_1 (
    .in0(in1[31:16]), .in1(in1[15:0]), .out(multiplexer_1_out), .sel(nor_1_out[4]));
  Comparator #(.mode("unsigned")) comparator_2 (
    .a(multiplexer_1_out[15:8]), .b({8{1'b0}}), .eq(nor_1_out[3]));  // open: gt, lt
  Multiplexer #(.width(8)) multiplexer_2 (
    .in0(multiplexer_1_out[15:8]), .in1(multiplexer_1_out[7:0]), .out(multiplexer_2_out), .sel(nor_1_out[3]));
  Comparator #(.mode("unsigned"), .width(4)) comparator_3 (
    .a(multiplexer_2_out[7:4]), .b(4'b0000), .eq(nor_1_out[2]));  // open: gt, lt
  Multiplexer #(.width(4)) multiplexer_3 (
    .in0(multiplexer_2_out[7:4]), .in1(multiplexer_2_out[3:0]), .out(multiplexer_3_out), .sel(nor_1_out[2]));
  Comparator #(.mode("unsigned"), .width(2)) comparator_4 (
    .a(multiplexer_3_out[3:2]), .b(2'b00), .eq(nor_1_out[1]));  // open: gt, lt
  nor nor_1 (nor_1_out[0], 1'b0, multiplexer_4_out[1]);
  Multiplexer #(.width(2)) multiplexer_4 (
    .in0(multiplexer_3_out[3:2]), .in1(multiplexer_3_out[1:0]), .out(multiplexer_4_out), .sel(nor_1_out[1]));
  not not_1 (not_1_out, multiplexer_4_out[1]);
  not not_2 (not_2_out, multiplexer_4_out[0]);
  Multiplexer multiplexer_5 (.in0(not_1_out), .in1(not_2_out), .out(multiplexer_5_out), .sel(nor_1_out[0]));
  Adder #(.width(6)) adder_1 (.a({1'b0, nor_1_out}), .b(bit_extender_1_out), .out(out1));  // open: cin, cout
  assign bit_extender_1_out = {{5{1'b0}}, multiplexer_5_out};  // Bit_Extender bit_extender_1
endmodule

module clo (
  input  [31:0] in1,
  output [5:0] out1
);

  wire multiplexer_5_out;
  wire [1:0] multiplexer_4_out;
  wire [3:0] multiplexer_3_out;
  wire [4:0] and_1_out;
  wire [5:0] bit_extender_1_out;
  wire [7:0] multiplexer_2_out;
  wire [15:0] multiplexer_1_out;

  Comparator #(.mode("unsigned"), .width(16)) comparator_1 (
    .a(in1[31:16]), .b({16{1'b1}}), .eq(and_1_out[4]));  // open: gt, lt
  Multiplexer #(.width(16)) multiplexer_1 (
    .in0(in1[31:16]), .in1(in1[15:0]), .out(multiplexer_1_out), .sel(and_1_out[4]));
  Comparator #(.mode("unsigned")) comparator_2 (
    .a(multiplexer_1_out[15:8]), .b({8{1'b1}}), .eq(and_1_out[3]));  // open: gt, lt
  Multiplexer #(.width(8)) multiplexer_2 (
    .in0(multiplexer_1_out[15:8]), .in1(multiplexer_1_out[7:0]), .out(multiplexer_2_out), .sel(and_1_out[3]));
  Comparator #(.mode("unsigned"), .width(4)) comparator_3 (
    .a(multiplexer_2_out[7:4]), .b(4'b1111), .eq(and_1_out[2]));  // open: gt, lt
  Multiplexer #(.width(4)) multiplexer_3 (
    .in0(multiplexer_2_out[7:4]), .in1(multiplexer_2_out[3:0]), .out(multiplexer_3_out), .sel(and_1_out[2]));
  Comparator #(.mode("unsigned"), .width(2)) comparator_4 (
    .a(multiplexer_3_out[3:2]), .b(2'b11), .eq(and_1_out[1]));  // open: gt, lt
  and and_1 (and_1_out[0], 1'b1, multiplexer_4_out[1]);
  Multiplexer #(.width(2)) multiplexer_4 (
    .in0(multiplexer_3_out[3:2]), .in1(multiplexer_3_out[1:0]), .out(multiplexer_4_out), .sel(and_1_out[1]));
  Multiplexer multiplexer_5 (
    .in0(multiplexer_4_out[1]), .in1(multiplexer_4_out[0]), .out(multiplexer_5_out), .sel(and_1_out[0]));
  Adder #(.width(6)) adder_1 (.a({1'b0, and_1_out}), .b(bit_extender_1_out), .out(out1));  // open: cin, cout
  assign bit_extender_1_out = {{5{1'b0}}, multiplexer_5_out};  // Bit_Extender bit_extender_1
endmodule

module add_sub (
  input  c_in,
  input  sub_notAdd,
  input  [31:0] in1,
  input  [31:0] in2,
  output [31:0] s,
  output c
);

  wire adder_1_cout, adder_2_cout, adder_3_cout, adder_4_cout, adder_5_cout, adder_6_cout, adder_7_cout,
       adder_8_cout, adder_9_cout, adder_10_cout, adder_11_cout, adder_12_cout, adder_13_cout, adder_14_cout,
       adder_15_cout, multiplexer_2_out, multiplexer_4_out, multiplexer_6_out, multiplexer_8_out,
       multiplexer_10_out, multiplexer_14_out;
  wire [3:0] adder_1_out, adder_2_out, adder_3_out, adder_4_out, adder_5_out, adder_6_out, adder_7_out,
       adder_8_out, adder_9_out, adder_10_out, adder_11_out, adder_12_out, adder_13_out, adder_14_out;
  wire [31:0] bit_extender_1_out, xor_1_out;

  assign xor_1_out = in2 ^ bit_extender_1_out;  // XOR_Gate xor_1, 32 bits wide
  Adder #(.width(4)) adder_1 (.a(xor_1_out[11:8]), .b(in1[11:8]), .out(adder_1_out), .cin(1'b0), .cout(adder_1_cout));
  Adder #(.width(4)) adder_2 (.a(xor_1_out[15:12]), .b(in1[15:12]), .out(adder_2_out), .cin(1'b0), .cout(adder_2_cout));
  Adder #(.width(4)) adder_3 (.a(xor_1_out[19:16]), .b(in1[19:16]), .out(adder_3_out), .cin(1'b0), .cout(adder_3_cout));
  Adder #(.width(4)) adder_4 (.a(xor_1_out[23:20]), .b(in1[23:20]), .out(adder_4_out), .cin(1'b0), .cout(adder_4_cout));
  Adder #(.width(4)) adder_5 (.a(xor_1_out[27:24]), .b(in1[27:24]), .out(adder_5_out), .cin(1'b0), .cout(adder_5_cout));
  Adder #(.width(4)) adder_6 (.a(xor_1_out[31:28]), .b(in1[31:28]), .out(adder_6_out), .cin(1'b0), .cout(adder_6_cout));
  assign bit_extender_1_out = {{31{sub_notAdd}}, sub_notAdd};  // Bit_Extender bit_extender_1
  Adder #(.width(4)) adder_7 (.a(xor_1_out[7:4]), .b(in1[7:4]), .out(adder_7_out), .cin(1'b0), .cout(adder_7_cout));
  Adder #(.width(4)) adder_8 (.a(xor_1_out[7:4]), .b(in1[7:4]), .out(adder_8_out), .cin(1'b1), .cout(adder_8_cout));
  Adder #(.width(4)) adder_9 (.a(xor_1_out[11:8]), .b(in1[11:8]), .out(adder_9_out), .cin(1'b1), .cout(adder_9_cout));
  Adder #(.width(4)) adder_10 (
    .a(xor_1_out[15:12]), .b(in1[15:12]), .out(adder_10_out), .cin(1'b1), .cout(adder_10_cout));
  Adder #(.width(4)) adder_11 (
    .a(xor_1_out[19:16]), .b(in1[19:16]), .out(adder_11_out), .cin(1'b1), .cout(adder_11_cout));
  Adder #(.width(4)) adder_12 (
    .a(xor_1_out[23:20]), .b(in1[23:20]), .out(adder_12_out), .cin(1'b1), .cout(adder_12_cout));
  Adder #(.width(4)) adder_13 (
    .a(xor_1_out[27:24]), .b(in1[27:24]), .out(adder_13_out), .cin(1'b1), .cout(adder_13_cout));
  Adder #(.width(4)) adder_14 (
    .a(xor_1_out[31:28]), .b(in1[31:28]), .out(adder_14_out), .cin(1'b1), .cout(adder_14_cout));
  Adder #(.width(4)) adder_15 (.a(xor_1_out[3:0]), .b(in1[3:0]), .out(s[3:0]), .cin(c_in), .cout(adder_15_cout));
  Multiplexer #(.width(4)) multiplexer_1 (
    .in0(adder_1_out), .in1(adder_9_out), .out(s[11:8]), .sel(multiplexer_14_out));
  Multiplexer multiplexer_2 (.in0(adder_1_cout), .in1(adder_9_cout), .out(multiplexer_2_out), .sel(multiplexer_14_out));
  Multiplexer #(.width(4)) multiplexer_3 (
    .in0(adder_2_out), .in1(adder_10_out), .out(s[15:12]), .sel(multiplexer_2_out));
  Multiplexer multiplexer_4 (.in0(adder_2_cout), .in1(adder_10_cout), .out(multiplexer_4_out), .sel(multiplexer_2_out));
  Multiplexer #(.width(4)) multiplexer_5 (
    .in0(adder_3_out), .in1(adder_11_out), .out(s[19:16]), .sel(multiplexer_4_out));
  Multiplexer multiplexer_6 (.in0(adder_3_cout), .in1(adder_11_cout), .out(multiplexer_6_out), .sel(multiplexer_4_out));
  Multiplexer #(.width(4)) multiplexer_7 (
    .in0(adder_4_out), .in1(adder_12_out), .out(s[23:20]), .sel(multiplexer_6_out));
  Multiplexer multiplexer_8 (.in0(adder_4_cout), .in1(adder_12_cout), .out(multiplexer_8_out), .sel(multiplexer_6_out));
  Multiplexer #(.width(4)) multiplexer_9 (
    .in0(adder_5_out), .in1(adder_13_out), .out(s[27:24]), .sel(multiplexer_8_out));
  Multiplexer multiplexer_10 (
    .in0(adder_5_cout), .in1(adder_13_cout), .out(multiplexer_10_out), .sel(multiplexer_8_out));
  Multiplexer #(.width(4)) multiplexer_11 (
    .in0(adder_6_out), .in1(adder_14_out), .out(s[31:28]), .sel(multiplexer_10_out));
  Multiplexer multiplexer_12 (.in0(adder_6_cout), .in1(adder_14_cout), .out(c), .sel(multiplexer_10_out));
  Multiplexer #(.width(4)) multiplexer_13 (.in0(adder_7_out), .in1(adder_8_out), .out(s[7:4]), .sel(adder_15_cout));
  Multiplexer multiplexer_14 (.in0(adder_7_cout), .in1(adder_8_cout), .out(multiplexer_14_out), .sel(adder_15_cout));
endmodule

module mul (
  input  [31:0] multiplicand,
  input  [31:0] mutiplier,
  input  clk,
  input  strat,
  output done,
  output [63:0] result
);

  wire A0_c, A1_c;
  wire [1:0] A3_carry, register_2_q, register_2_q_2, register_2_q_3, register_2_q_4, register_2_q_5,
       register_2_q_6, register_2_q_7, register_2_q_8, register_2_q_9, register_2_q_10, register_2_q_11,
       register_2_q_12, register_2_q_13, register_2_q_14, register_2_q_15, register_2_q_16;
  wire [31:0] A0_s, A1_s, A2_s, A3_sum, A4_sum, A5_s, A7_s, bit_extender_2_out, carry_q, multiplexer_2_out,
       multiplexer_4_out, multiplexer_6_out, register_1_q, register_1_q_2, shifter_1_out, shifter_1_out_2,
       shifter_2_out, shifter_3_out, temp_res_q;
  wire [63:0] bit_extender_1_out, multiplexer_1_out, multiplexer_3_out, multiplexer_5_out, shifter_4_out,
       shifter_5_out;

  assign bit_extender_1_out = {{32{1'b0}}, multiplicand};  // Bit_Extender bit_extender_1
  Counter #(.max('he), .width(4)) counter_1 (
    .clr(strat), .load(strat), .clk(clk), .carry(done));  // open: up, count, D, Q
  Multiplexer #(.width(64)) multiplexer_1 (
    .in0(shifter_5_out), .in1(bit_extender_1_out), .out(multiplexer_1_out), .sel(strat));
  Multiplexer #(.width(32)) multiplexer_2 (.in0(shifter_3_out), .in1(mutiplier), .out(multiplexer_2_out), .sel(strat));
  Register #(.width(64)) register_1 (
    .D(multiplexer_1_out), .en(1'b1), .clk(clk), .Q({register_1_q_2, register_1_q}));  // open: clr
  Register #(.width(32)) register_2 (
    .D(multiplexer_2_out), .en(1'b1), .clk(clk),
    .Q({register_2_q_16, register_2_q_15, register_2_q_14, register_2_q_13, register_2_q_12, register_2_q_11, register_2_q_10, register_2_q_9, register_2_q_8, register_2_q_7, register_2_q_6, register_2_q_5, register_2_q_4, register_2_q_3, register_2_q_2, register_2_q}));  // open: clr
  Shifter #(.width(64)) shifter_1 (
    .in({register_1_q_2, register_1_q}), .\dist (6'b000001), .out({shifter_1_out_2, shifter_1_out}));
  Shifter #(.shift("lr"), .width(32)) shifter_2 (
    .in({register_2_q_16, register_2_q_15, register_2_q_14, register_2_q_13, register_2_q_12, register_2_q_11, register_2_q_10, register_2_q_9, register_2_q_8, register_2_q_7, register_2_q_6, register_2_q_5, register_2_q_4, register_2_q_3, register_2_q_2, register_2_q}),
    .\dist (5'b00001), .out(shifter_2_out));
  Shifter #(.shift("lr"), .width(32)) shifter_3 (.in(shifter_2_out), .\dist (5'b00001), .out(shifter_3_out));
  Shifter #(.width(64)) shifter_4 (.in({register_1_q_2, register_1_q}), .\dist (6'b000001), .out(shifter_4_out));
  Shifter #(.width(64)) shifter_5 (.in(shifter_4_out), .\dist (6'b000001), .out(shifter_5_out));
  carrySaveAdder A3 (.in1(register_1_q), .in2(shifter_1_out), .in3(result[31:0]), .sum(A3_sum), .carry(A3_carry));
  carrySaveAdder A4 (.in1(register_1_q_2), .in2(shifter_1_out_2), .in3(temp_res_q), .sum(A4_sum));  // open: carry
  carrySelectAdder A0 (.c_in(1'b0), .in1(register_1_q), .in2(result[31:0]), .s(A0_s), .c(A0_c));
  carrySelectAdder A7 (.c_in(A0_c), .in1(register_1_q_2), .in2(temp_res_q), .s(A7_s));  // open: c
  carrySelectAdder A1 (.c_in(1'b0), .in1(shifter_1_out), .in2(result[31:0]), .s(A1_s), .c(A1_c));
  carrySelectAdder A2 (.c_in(A1_c), .in1(shifter_1_out_2), .in2(temp_res_q), .s(A2_s));  // open: c
  assign bit_extender_2_out = {{30{1'b0}}, A3_carry};  // Bit_Extender bit_extender_2
  Multiplexer #(.select(2), .width(64)) multiplexer_3 (
    .in0({temp_res_q, result[31:0]}), .in1({A7_s, A0_s}), .in2({A2_s, A1_s}), .in3({A4_sum, A3_sum}),
    .out(multiplexer_3_out), .sel(register_2_q));
  carrySelectAdder A5 (.c_in(1'b0), .in1(bit_extender_2_out), .in2(carry_q), .s(A5_s));  // open: c
  Multiplexer #(.select(2), .width(32)) multiplexer_4 (
    .in0(carry_q), .in1(carry_q), .in2(carry_q), .in3(A5_s), .out(multiplexer_4_out), .sel(register_2_q));
  Multiplexer #(.width(64)) multiplexer_5 (
    .in0(multiplexer_3_out), .in1({64{1'b0}}), .out(multiplexer_5_out), .sel(strat));
  Multiplexer #(.width(32)) multiplexer_6 (
    .in0(multiplexer_4_out), .in1({32{1'b0}}), .out(multiplexer_6_out), .sel(strat));
  Register #(.width(64)) temp_res (
    .D(multiplexer_5_out), .en(1'b1), .clk(clk), .Q({temp_res_q, result[31:0]}));  // open: clr
  Register #(.width(32)) carry (.D(multiplexer_6_out), .en(1'b1), .clk(clk), .Q(carry_q));  // open: clr
  carrySelectAdder A6 (.c_in(1'b0), .in1(temp_res_q), .in2(carry_q), .s(result[63:32]));  // open: c
endmodule

module carrySelectAdder (
  input  c_in,
  input  [31:0] in1,
  input  [31:0] in2,
  output [31:0] s,
  output c
);

  wire adder_1_cout, adder_2_cout, adder_3_cout, adder_4_cout, adder_5_cout, adder_6_cout, adder_7_cout,
       adder_8_cout, adder_9_cout, adder_10_cout, adder_11_cout, adder_12_cout, adder_13_cout, adder_14_cout,
       adder_15_cout, multiplexer_2_out, multiplexer_4_out, multiplexer_6_out, multiplexer_8_out,
       multiplexer_10_out, multiplexer_14_out;
  wire [3:0] adder_1_out, adder_2_out, adder_3_out, adder_4_out, adder_5_out, adder_6_out, adder_7_out,
       adder_8_out, adder_9_out, adder_10_out, adder_11_out, adder_12_out, adder_13_out, adder_14_out;

  Adder #(.width(4)) adder_1 (.a(in2[11:8]), .b(in1[11:8]), .out(adder_1_out), .cin(1'b0), .cout(adder_1_cout));
  Adder #(.width(4)) adder_2 (.a(in2[15:12]), .b(in1[15:12]), .out(adder_2_out), .cin(1'b0), .cout(adder_2_cout));
  Adder #(.width(4)) adder_3 (.a(in2[19:16]), .b(in1[19:16]), .out(adder_3_out), .cin(1'b0), .cout(adder_3_cout));
  Adder #(.width(4)) adder_4 (.a(in2[23:20]), .b(in1[23:20]), .out(adder_4_out), .cin(1'b0), .cout(adder_4_cout));
  Adder #(.width(4)) adder_5 (.a(in2[27:24]), .b(in1[27:24]), .out(adder_5_out), .cin(1'b0), .cout(adder_5_cout));
  Adder #(.width(4)) adder_6 (.a(in2[31:28]), .b(in1[31:28]), .out(adder_6_out), .cin(1'b0), .cout(adder_6_cout));
  Adder #(.width(4)) adder_7 (.a(in2[7:4]), .b(in1[7:4]), .out(adder_7_out), .cin(1'b0), .cout(adder_7_cout));
  Adder #(.width(4)) adder_8 (.a(in2[7:4]), .b(in1[7:4]), .out(adder_8_out), .cin(1'b1), .cout(adder_8_cout));
  Adder #(.width(4)) adder_9 (.a(in2[11:8]), .b(in1[11:8]), .out(adder_9_out), .cin(1'b1), .cout(adder_9_cout));
  Adder #(.width(4)) adder_10 (.a(in2[15:12]), .b(in1[15:12]), .out(adder_10_out), .cin(1'b1), .cout(adder_10_cout));
  Adder #(.width(4)) adder_11 (.a(in2[19:16]), .b(in1[19:16]), .out(adder_11_out), .cin(1'b1), .cout(adder_11_cout));
  Adder #(.width(4)) adder_12 (.a(in2[23:20]), .b(in1[23:20]), .out(adder_12_out), .cin(1'b1), .cout(adder_12_cout));
  Adder #(.width(4)) adder_13 (.a(in2[27:24]), .b(in1[27:24]), .out(adder_13_out), .cin(1'b1), .cout(adder_13_cout));
  Adder #(.width(4)) adder_14 (.a(in2[31:28]), .b(in1[31:28]), .out(adder_14_out), .cin(1'b1), .cout(adder_14_cout));
  Adder #(.width(4)) adder_15 (.a(in2[3:0]), .b(in1[3:0]), .out(s[3:0]), .cin(c_in), .cout(adder_15_cout));
  Multiplexer #(.width(4)) multiplexer_1 (
    .in0(adder_1_out), .in1(adder_9_out), .out(s[11:8]), .sel(multiplexer_14_out));
  Multiplexer multiplexer_2 (.in0(adder_1_cout), .in1(adder_9_cout), .out(multiplexer_2_out), .sel(multiplexer_14_out));
  Multiplexer #(.width(4)) multiplexer_3 (
    .in0(adder_2_out), .in1(adder_10_out), .out(s[15:12]), .sel(multiplexer_2_out));
  Multiplexer multiplexer_4 (.in0(adder_2_cout), .in1(adder_10_cout), .out(multiplexer_4_out), .sel(multiplexer_2_out));
  Multiplexer #(.width(4)) multiplexer_5 (
    .in0(adder_3_out), .in1(adder_11_out), .out(s[19:16]), .sel(multiplexer_4_out));
  Multiplexer multiplexer_6 (.in0(adder_3_cout), .in1(adder_11_cout), .out(multiplexer_6_out), .sel(multiplexer_4_out));
  Multiplexer #(.width(4)) multiplexer_7 (
    .in0(adder_4_out), .in1(adder_12_out), .out(s[23:20]), .sel(multiplexer_6_out));
  Multiplexer multiplexer_8 (.in0(adder_4_cout), .in1(adder_12_cout), .out(multiplexer_8_out), .sel(multiplexer_6_out));
  Multiplexer #(.width(4)) multiplexer_9 (
    .in0(adder_5_out), .in1(adder_13_out), .out(s[27:24]), .sel(multiplexer_8_out));
  Multiplexer multiplexer_10 (
    .in0(adder_5_cout), .in1(adder_13_cout), .out(multiplexer_10_out), .sel(multiplexer_8_out));
  Multiplexer #(.width(4)) multiplexer_11 (
    .in0(adder_6_out), .in1(adder_14_out), .out(s[31:28]), .sel(multiplexer_10_out));
  Multiplexer multiplexer_12 (.in0(adder_6_cout), .in1(adder_14_cout), .out(c), .sel(multiplexer_10_out));
  Multiplexer #(.width(4)) multiplexer_13 (.in0(adder_7_out), .in1(adder_8_out), .out(s[7:4]), .sel(adder_15_cout));
  Multiplexer multiplexer_14 (.in0(adder_7_cout), .in1(adder_8_cout), .out(multiplexer_14_out), .sel(adder_15_cout));
endmodule

module carrySaveAdder (
  input  [31:0] in1,
  input  [31:0] in2,
  input  [31:0] in3,
  output [31:0] sum,
  output [1:0] carry
);

  wire A_c;
  wire [31:0] and_1_out, and_2_out, and_3_out, or_1_out, xor_1_out, xor_2_out;

  assign xor_1_out = in1 ^ in2;  // XOR_Gate xor_1, 32 bits wide
  assign and_1_out = in1 & in2;  // AND_Gate and_1, 32 bits wide
  assign and_2_out = in2 & in3;  // AND_Gate and_2, 32 bits wide
  assign and_3_out = in1 & in3;  // AND_Gate and_3, 32 bits wide
  assign xor_2_out = xor_1_out ^ in3;  // XOR_Gate xor_2, 32 bits wide
  assign or_1_out = and_1_out | and_2_out | and_3_out;  // OR_Gate or_1, 32 bits wide
  carrySelectAdder A (.c_in(1'b0), .in1(xor_2_out), .in2({or_1_out[30:0], 1'b0}), .s(sum), .c(A_c));
  xor xor_3 (carry[0], A_c, or_1_out[31]);
  and and_4 (carry[1], A_c, or_1_out[31]);
endmodule

module div (
  input  clk,
  input  start,
  input  [31:0] dividend,
  input  [31:0] divisor,
  output [31:0] remainder,
  output [31:0] quotient,
  output done
);

  wire comparator_1_eq, not_1_out, not_2_out;
  wire [0:0] comparator_2_lt;
  wire [31:0] b_q, counter_q, multiplexer_1_out, multiplexer_2_out, multiplexer_3_out, multiplexer_4_out,
       multiplexer_5_out, subtractor_1_out, subtractor_2_out;
  wire [63:0] shifter_1_out;

  Multiplexer #(.select(2), .width(32)) multiplexer_1 (
    .in0(shifter_1_out[63:32]), .in1(shifter_1_out[63:32]), .in2(subtractor_2_out), .in3(remainder),
    .out(multiplexer_1_out), .sel({counter_q[0], comparator_2_lt[0]}));
  Multiplexer #(.select(2), .width(32)) multiplexer_2 (
    .in0(shifter_1_out[31:0]), .in1(shifter_1_out[31:0]), .in2({quotient[31:1], 1'b1}), .in3(quotient),
    .out(multiplexer_2_out), .sel({counter_q[0], comparator_2_lt[0]}));
  Multiplexer #(.width(32)) multiplexer_3 (
    .in0(multiplexer_1_out), .in1({32{1'b0}}), .out(multiplexer_3_out), .sel(start));
  Multiplexer #(.width(32)) multiplexer_4 (
    .in0(multiplexer_2_out), .in1(dividend), .out(multiplexer_4_out), .sel(start));
  Multiplexer #(.width(32)) multiplexer_5 (.in0(subtractor_1_out), .in1(32'h40), .out(multiplexer_5_out), .sel(start));
  Register #(.width(32)) a (.D(multiplexer_3_out), .en(not_1_out), .clk(clk), .Q(remainder));  // open: clr
  Register #(.width(32)) b (.D(divisor), .en(start), .clk(clk), .Q(b_q));  // open: clr
  Register #(.width(32)) q (.D(multiplexer_4_out), .en(not_1_out), .clk(clk), .Q(quotient));  // open: clr
  Register #(.width(32)) counter (.D(multiplexer_5_out), .en(not_1_out), .clk(clk), .Q(counter_q));  // open: clr
  Subtractor #(.width(32)) subtractor_1 (.a(counter_q), .b(32'h1), .out(subtractor_1_out));  // open: bin, bout
  Shifter #(.width(64)) shifter_1 (.in({remainder, quotient}), .\dist (6'b000001), .out(shifter_1_out));
  Comparator #(.width(32)) comparator_1 (.a(counter_q), .b({32{1'b0}}), .eq(comparator_1_eq));  // open: gt, lt
  not not_1 (not_1_out, done);
  Comparator #(.mode("unsigned"), .width(32)) comparator_2 (
    .a(remainder), .b(b_q), .lt(comparator_2_lt[0]));  // open: gt, eq
  not not_2 (not_2_out, start);
  Subtractor #(.width(32)) subtractor_2 (.a(remainder), .b(b_q), .out(subtractor_2_out));  // open: bin, bout
  and and_1 (done, comparator_1_eq, not_2_out);
endmodule

module srlShift (
  input  [31:0] in1,
  input  [4:0] shift,
  output [31:0] out1
);

  Multiplexer #(.select(5), .width(32)) multiplexer_1 (
    .in0(in1), .in1({1'b0, in1[31:1]}), .in2({2'b00, in1[31:2]}), .in3({3'b000, in1[31:3]}),
    .in4({4'b0000, in1[31:4]}), .in5({{5{1'b0}}, in1[31:5]}), .in6({{6{1'b0}}, in1[31:6]}),
    .in7({{7{1'b0}}, in1[31:7]}), .in8({{8{1'b0}}, in1[31:8]}), .in9({{9{1'b0}}, in1[31:9]}),
    .in10({{10{1'b0}}, in1[31:10]}), .in11({{11{1'b0}}, in1[31:11]}), .in12({{12{1'b0}}, in1[31:12]}),
    .in13({{13{1'b0}}, in1[31:13]}), .in14({{14{1'b0}}, in1[31:14]}), .in15({{15{1'b0}}, in1[31:15]}),
    .in16({{16{1'b0}}, in1[31:16]}), .in17({{17{1'b0}}, in1[31:17]}), .in18({{18{1'b0}}, in1[31:18]}),
    .in19({{19{1'b0}}, in1[31:19]}), .in20({{20{1'b0}}, in1[31:20]}), .in21({{21{1'b0}}, in1[31:21]}),
    .in22({{22{1'b0}}, in1[31:22]}), .in23({{23{1'b0}}, in1[31:23]}), .in24({{24{1'b0}}, in1[31:24]}),
    .in25({{25{1'b0}}, in1[31:25]}), .in26({{26{1'b0}}, in1[31:26]}), .in27({{27{1'b0}}, in1[31:27]}),
    .in28({{28{1'b0}}, in1[31:28]}), .in29({{29{1'b0}}, in1[31:29]}), .in30({{30{1'b0}}, in1[31:30]}),
    .in31({{31{1'b0}}, in1[31]}), .out(out1), .sel(shift));
endmodule
